// Logisim project 7-6.circ as structural Verilog
module _4X4_Ram (
  input  in_1,
  input  in_2,
  input  in_3,
  input  in_4,
  output [3:0] out_5,
  output [3:0] out_6,
  output [3:0] out_7,
  output [3:0] out_8
);
endmodule

module _8X8_Ram (
  input  a2,
  input  a1,
  input  a0,
  input  sel,
  input  r_w
);

  wire and_1_out, and_2_out, not_1_out;
  wire [3:0] n4x4_ram_1_out_5, n4x4_ram_1_out_6, n4x4_ram_1_out_7, n4x4_ram_1_out_8, n4x4_ram_2_out_5,
       n4x4_ram_2_out_6, n4x4_ram_2_out_7, n4x4_ram_2_out_8, n4x4_ram_3_out_5, n4x4_ram_3_out_6,
       n4x4_ram_3_out_7, n4x4_ram_3_out_8, n4x4_ram_4_out_5, n4x4_ram_4_out_6, n4x4_ram_4_out_7,
       n4x4_ram_4_out_8;

  not not_1 (not_1_out, a2);
  and and_1 (and_1_out, sel, not_1_out);
  and and_2 (and_2_out, sel, a2);
  _4X4_Ram u_4x4_ram_1 (
    .in_1(a0), .in_2(a1), .in_3(and_1_out), .in_4(r_w), .out_5(n4x4_ram_1_out_5), .out_6(n4x4_ram_1_out_6),
    .out_7(n4x4_ram_1_out_7), .out_8(n4x4_ram_1_out_8));
  _4X4_Ram u_4x4_ram_2 (
    .in_1(a0), .in_2(a1), .in_3(and_2_out), .in_4(r_w), .out_5(n4x4_ram_2_out_5), .out_6(n4x4_ram_2_out_6),
    .out_7(n4x4_ram_2_out_7), .out_8(n4x4_ram_2_out_8));
  _4X4_Ram u_4x4_ram_3 (
    .in_1(a0), .in_2(a1), .in_3(and_1_out), .in_4(r_w), .out_5(n4x4_ram_3_out_5), .out_6(n4x4_ram_3_out_6),
    .out_7(n4x4_ram_3_out_7), .out_8(n4x4_ram_3_out_8));
  _4X4_Ram u_4x4_ram_4 (
    .in_1(a0), .in_2(a1), .in_3(and_2_out), .in_4(r_w), .out_5(n4x4_ram_4_out_5), .out_6(n4x4_ram_4_out_6),
    .out_7(n4x4_ram_4_out_7), .out_8(n4x4_ram_4_out_8));

  // Notes on the sheet:
  //   [7:4]
  //   [3:0]
endmodule
